# Fritzing sketch flowtime-flag (saved by Fritzing 0.9.3b)

parts:
  M1 = Dagu DGServo 9g (Top view) [part_number=RS001B]
  U1 = NodeMCU V3.0

nets:
  GND: M1.gnd, U1.GND
  VCC: M1.vcc, U1.Vin
  N1: M1.pulse, U1.D7

custom parts:
  NodeMCU V3.0: ESP8266 based NodeMCU
